# Fritzing sketch led_photo (saved by Fritzing 0.8.7b)
breadboards: 1

parts:
  LDR = Photocell (LDR) [package=THT]
  part = Resistor [tolerance=±5% resistance=10k package=THT]
  part_2 = Resistor [tolerance=±5% resistance=330 package=THT]
  LED = LED - 5mm [color="Red (633nm)" package="5 mm [THT]"]
  Arduino = Arduino Uno (Rev3)

nets:
  N1: LDR.pin_0, Arduino.5V
  N2: LDR.pin_1, part.Pin_0, Arduino.A0
  N3: part.Pin_1, part_2.Pin_1, Arduino.GND
  N4: part_2.Pin_0, LED.cathode
  N5: LED.anode, Arduino.D11_PWM/MOSI
