# Fritzing sketch single_traffic_light (saved by Fritzing 0.8.7b)
breadboards: 1

parts:
  Part1 = Arduino Uno (Rev3)
  part = LED - 5mm [color="Red (633nm)" package="5 mm [THT]"]
  part_2 = Resistor [tolerance=±5% resistance=330 package=THT]
  part_3 = LED - 5mm [color="Yellow (585nm)" package="5 mm [THT]"]
  part_4 = Resistor [tolerance=±5% resistance=330 package=THT]
  part_5 = LED - 5mm [color="Green (555nm)" package="5 mm [THT]"]
  part_6 = Resistor [tolerance=±5% resistance=330 package=THT]

nets:
  N1: Part1.GND, part_2.Pin_0, part_4.Pin_0, part_6.Pin_0
  N2: Part1.D4, part_5.anode
  N3: Part1.D5_PWM, part_3.anode
  N4: Part1.D6_PWM, part.anode
  N5: part.cathode, part_4.Pin_1
  N6: part_2.Pin_1, part_5.cathode
  N7: part_3.cathode, part_6.Pin_1
