# Fritzing sketch two_traffic_lights (saved by Fritzing 0.8.7b)
breadboards: 1

parts:
  Part1 = Arduino Uno (Rev3)
  R2 = Resistor [tolerance=±5% resistance=10k package=THT]  # not connected
  LED1 = LED - 5mm [color="Red (633nm)" package="5 mm [THT]"]
  R3 = Resistor [tolerance=±5% resistance=330 package=THT]
  R4 = Resistor [tolerance=±5% resistance=330 package=THT]
  LED2 = LED - 5mm [color="Yellow (585nm)" package="5 mm [THT]"]
  LED3 = LED - 5mm [color="Green (555nm)" package="5 mm [THT]"]
  LED4 = LED - 5mm [color="Green (555nm)" package="5 mm [THT]"]
  R6 = Resistor [tolerance=±5% resistance=330 package=THT]
  R7 = Resistor [tolerance=±5% resistance=330 package=THT]
  LED5 = LED - 5mm [color="Yellow (585nm)" package="5 mm [THT]"]
  R8 = Resistor [tolerance=±5% resistance=330 package=THT]
  LED6 = LED - 5mm [color="Red (633nm)" package="5 mm [THT]"]
  R9 = Resistor [tolerance=±5% resistance=330 package=THT]

nets:
  N1: Part1.D9_PWM, LED3.anode
  N2: Part1.D10_PWM/SS, LED2.anode
  N3: Part1.D11_PWM/MOSI, LED1.anode
  N4: Part1.D4, LED4.anode
  N5: Part1.D5_PWM, LED5.anode
  N6: Part1.D6_PWM, LED6.anode
  N7: Part1.GND, R7.Pin_0, R8.Pin_0, R9.Pin_0
  N8: LED1.cathode, R3.Pin_0
  N9: R4.Pin_0, LED2.cathode
  N10: LED3.cathode, R6.Pin_0
  N11: LED4.cathode, R7.Pin_1
  N12: LED5.cathode, R8.Pin_1
  N13: LED6.cathode, R9.Pin_1
