# Fritzing sketch two_traffic_lights_sensor_schem (saved by Fritzing 0.8.7b)
breadboards: 1

parts:
  Part2 = Arduino Uno (Rev3)
  part = LED - 5mm [color="Red (633nm)" package="5 mm [THT]"]
  part_2 = LED - 5mm [color="Yellow (585nm)" package="5 mm [THT]"]
  part_3 = LED - 5mm [color="Green (555nm)" package="5 mm [THT]"]
  part_4 = Resistor [tolerance=±5% resistance=330 package=THT]
  part_5 = Resistor [tolerance=±5% resistance=330 package=THT]
  part_6 = Resistor [tolerance=±5% resistance=330 package=THT]
  part_7 = LED - 5mm [color="Red (633nm)" package="5 mm [THT]"]
  part_8 = LED - 5mm [color="Yellow (585nm)" package="5 mm [THT]"]
  part_9 = LED - 5mm [color="Green (555nm)" package="5 mm [THT]"]
  part_10 = Resistor [tolerance=±5% resistance=330 package=THT]
  part_11 = Resistor [tolerance=±5% resistance=330 package=THT]
  part_12 = Resistor [tolerance=±5% resistance=330 package=THT]
  LDR = Photocell (LDR) [package=THT]
  part_13 = Resistor [tolerance=±5% resistance=10k package=THT]

nets:
  N1: Part2.A0, LDR.pin_0, part_13.Pin_1
  N2: Part2.D9_PWM, part_9.anode
  N3: Part2.D10_PWM/SS, part_8.anode
  N4: Part2.D11_PWM/MOSI, part_7.anode
  N5: Part2.GND, part_4.Pin_0, part_5.Pin_0, part_6.Pin_0, part_10.Pin_0, part_11.Pin_0, part_12.Pin_0, part_13.Pin_0
  N6: Part2.D4, part_3.anode
  N7: Part2.D5_PWM, part_2.anode
  N8: Part2.D6_PWM, part.anode
  N9: Part2.5V, LDR.pin_1
  N10: part.cathode, part_4.Pin_1
  N11: part_2.cathode, part_6.Pin_1
  N12: part_3.cathode, part_5.Pin_1
  N13: part_7.cathode, part_10.Pin_1
  N14: part_8.cathode, part_11.Pin_1
  N15: part_9.cathode, part_12.Pin_1
